// Logisim project Master.circ as structural Verilog: 1 circuit, main circuit main
module main (
);

  wire and_6_out, and_7_out, and_8_out, and_9_out, and_10_out, and_11_out, clock_1_out, Group_0, Group_1,
       Group_2, Group_3, Group_4, not_1_out, not_2_out, not_3_out, not_4_out, not_5_out, not_6_out,
       not_7_out, not_8_out, not_9_out, not_10_out, not_11_out, not_12_out, not_13_out, not_14_out,
       not_15_out;
  wire [3:0] counter_1_q, Dest, Group, Instruction, Source;

  Counter #(.width(4), .max('hf)) counter_1 (.Q(counter_1_q), .clk(clock_1_out));  // open: load, D, count, carry, clr
  Clock clock_1 (.out(clock_1_out));
  not not_1 (not_1_out, Group[3]);
  not not_2 (not_2_out, Group[1]);
  not not_3 (not_3_out, Group[0]);
  not not_4 (not_4_out, Group[2]);
  and and_1 (Group_0, not_3_out, not_2_out, not_4_out, not_1_out);
  not not_5 (not_5_out, Group[0]);
  not not_6 (not_6_out, Group[3]);
  not not_7 (not_7_out, Group[2]);
  not not_8 (not_8_out, Group[1]);
  and and_2 (Group_2, not_5_out, Group[1], not_11_out, not_10_out);
  and and_3 (Group_1, Group[0], not_8_out, not_7_out, not_6_out);
  not not_9 (not_9_out, Group[3]);
  not not_10 (not_10_out, Group[3]);
  not not_11 (not_11_out, Group[2]);
  not not_12 (not_12_out, Group[2]);
  and and_4 (Group_3, Group[0], Group[1], not_12_out, not_9_out);
  ROM #(.addrWidth(4), .dataWidth(16)) rom_1 (
    .addr(counter_1_q), .data({Group, Instruction, Source, Dest}));  // open: sel
  not not_13 (not_13_out, Group[3]);
  not not_14 (not_14_out, Group[0]);
  not not_15 (not_15_out, Group[1]);
  and and_5 (Group_4, not_14_out, not_15_out, Group[2], not_13_out);
  and and_6 (and_6_out, Group_2, Instruction[0], Instruction[1], Instruction[2], ~Instruction[3]);  // AND_Gate
  LED led_1 (.in(and_6_out));
  and and_7 (and_7_out, Group_2, ~Instruction[0], Instruction[1], ~Instruction[2], ~Instruction[3]);  // AND_Gate
  and and_8 (and_8_out, Group_2, Instruction[0], ~Instruction[1], ~Instruction[2], Instruction[3]);  // AND_Gate
  LED led_2 (.in(and_7_out));
  LED led_3 (.in(and_8_out));
  and and_9 (and_9_out, Group_2, ~Instruction[0], ~Instruction[1], ~Instruction[2], Instruction[3]);  // AND_Gate
  LED led_4 (.in(and_9_out));
  and and_10 (and_10_out, Group_3, Instruction[0], Instruction[1], ~Instruction[2], ~Instruction[3]);  // AND_Gate
  LED led_5 (.in(and_10_out));
  and and_11 (and_11_out, Group_3, ~Instruction[0], Instruction[1], Instruction[2], ~Instruction[3]);  // AND_Gate
  LED led_6 (.in(and_11_out));

  // Notes on the sheet:
  //   help
  //   contents of rom_1 (hex, n*v repeats v):
  //   2712 2985 11c7 2264 0 2831 3323 3648
  //   help
  //   Add
  //   RRmov
  //   Mul
  //   Sub
  //   ldm
  //   stm
endmodule
